# Fritzing sketch GardenWAM (saved by Fritzing 0.9.3b)

parts:
  ADC1 = MCP3008 [package=dil16]
  Raspberry_Pi1 = Raspberry Pi Zero

nets:
  GND: ADC1.DGND, ADC1.AGND, Raspberry_Pi1.pin_6, Raspberry_Pi1.pin_9, Raspberry_Pi1.pin_14, Raspberry_Pi1.pin_20, Raspberry_Pi1.pin_25, Raspberry_Pi1.pin_30, Raspberry_Pi1.pin_34, Raspberry_Pi1.pin_39
  CE0: ADC1.CS/SHDN, Raspberry_Pi1.pin_24
  MOSI: ADC1.Din, Raspberry_Pi1.pin_19
  MISO: ADC1.Dout, Raspberry_Pi1.pin_21
  SCLK: ADC1.CLK, Raspberry_Pi1.pin_23
  3.3V: ADC1.VREF, ADC1.VDD, Raspberry_Pi1.pin_1, Raspberry_Pi1.pin_17
  5V: Raspberry_Pi1.pin_2, Raspberry_Pi1.pin_4
  SDA: Raspberry_Pi1.pin_3
  SCL: Raspberry_Pi1.pin_5
